# Fritzing sketch Diagram (saved by Fritzing 0.9.9b)
breadboards: 1

parts:
  Pololu_A1 = Pololu A4988 [package=SO16]
  Pololu_A2 = Pololu A4988 [package=SO16]
  Pololu_A3 = Pololu A4988 [package=SO16]
  J2 = Power Jack [package=power_jack_pth_lock]

nets:
  N1: Pololu_A1.RESET, Pololu_A1.SLEEP
  N2: Pololu_A1.GND#8, Pololu_A2.GND#8, Pololu_A3.GND#8
  VDD: Pololu_A1.VDD, Pololu_A2.VDD, Pololu_A3.VDD
  N3: Pololu_A1.GND#14, Pololu_A2.GND#14, Pololu_A3.GND#14, J2.GND
  N4: Pololu_A1.VMOT, Pololu_A2.VMOT, Pololu_A3.VMOT, J2.PWR
  N5: Pololu_A2.RESET, Pololu_A2.SLEEP
  N6: Pololu_A3.RESET, Pololu_A3.SLEEP

notes:
  Motor Power Source
  Motor Controller
  5V
  GND
  Power Source
  Signal Wires
  DIR
  STEP
  SLEEP
  ←  same as
  same as  →
  2B
  2A
  1A
  1B
  Motor Wires
